// Logisim project t3.circ as structural Verilog: 1 circuit, main circuit main
module main (
  output Q1,
  output Q2,
  output Q3
);

  wire and_1_out, clock_1_out;

  Clock clock_1 (.out(clock_1_out));
  T_Flip_Flop t_ff_1 (.T(1'b1), .clk(clock_1_out), .Q(Q1));  // open: Qn, reset, preset
  T_Flip_Flop t_ff_2 (.T(Q1), .clk(clock_1_out), .Q(Q2));  // open: Qn, reset, preset
  and and_1 (and_1_out, Q1, Q2);
  T_Flip_Flop t_ff_3 (.T(and_1_out), .clk(clock_1_out), .Q(Q3));  // open: Qn, reset, preset
endmodule
